# Fritzing sketch CIRC03 (saved by Fritzing 0.9.2b)
circuit board: 1.67628cm x 1.70089cm
breadboards: 1

parts:
  Part1 = Arduino Uno (Rev3)
  resistor = Resistor [tolerance=±5% resistance=2.2k package=THT]
  Diode = Rectifier Diode [part_number=1N4001 package="300 mil [THT]"]
  Motor = DC Motor
  Transistor = NPN-Transistor [part_number=P2N2222AG package="TO92 [THT]"]
  C1 = Electrolytic Capacitor [capacitance=0.22mF voltage=16V package="100 mil [THT, electrolytic]"]
  Pad1 = Pad [width=2.04 height=2.04 connect=center]  # not connected
  Pad2 = Pad [width=2.04 height=2.04 connect=center]
  Pad3 = Pad [width=2.04 height=2.04 connect=center]
  Pad4 = Pad [width=2.04 height=2.04 connect=center]
  Pad5 = Pad [width=2.04 height=2.04 connect=center]  # not connected
  Pad6 = Pad [width=2.04 height=2.04 connect=center]  # not connected

nets:
  pin 9: Part1.D9_PWM, resistor.Pin_1, Pad2.pad
  5V: Part1.5V, Diode.cathode, Motor.pin_1, C1.+, Pad3.pad
  GND: Part1.GND, Transistor.E, C1.-, Pad4.pad
  N1: resistor.Pin_0, Transistor.B
  N2: Diode.anode, Motor.pin_2, Transistor.C

notes:
  Transistor
  (P2N2222A)
  2.2Kohm
  optional
  Capacitor
  220µF
  longer
  lead
  diode
  (ground) (-)
  Collector
  Base
  Emitter
  Arduino
